// Logisim project cpu.circ as structural Verilog: 4 circuits, main circuit pc
module main (
);

  wire branch_equal, clock_1_out, imi_sel, load_sel, set_pc_sel, store_sel;
  wire [4:0] control_unit_1_rd, control_unit_1_rs1, control_unit_1_rs2;
  wire [31:0] adder_1_out, control_unit_1_imm, multiplexer_1_out, multiplexer_2_out, multiplexer_3_out,
       pc_1_q, ram_1_dout, reg_file_1_q1, reg_file_1_q2, rom_1_data;

  Clock clock_1 (.out(clock_1_out));
  ROM #(.addrWidth(24), .dataWidth(32)) rom_1 (.addr(pc_1_q[25:2]), .data(rom_1_data));
  pc pc_1 (.d(adder_1_out), .clk(clock_1_out), .set_pc(set_pc_sel), .q(pc_1_q));
  control_unit control_unit_1 (
    .branch_equal(branch_equal), .inst(rom_1_data), .rd(control_unit_1_rd), .rs1(control_unit_1_rs1),
    .rs2(control_unit_1_rs2), .imi_sel(imi_sel), .load_sel(load_sel), .store_sel(store_sel),
    .set_pc_sel(set_pc_sel), .imm(control_unit_1_imm));
  Multiplexer #(.width(32)) multiplexer_1 (
    .in0(adder_1_out), .in1(ram_1_dout), .out(multiplexer_1_out), .sel(load_sel));
  reg_file reg_file_1 (
    .d(multiplexer_1_out), .rd(control_unit_1_rd), .rs1(control_unit_1_rs1), .rs2(control_unit_1_rs2),
    .clk(clock_1_out), .q1(reg_file_1_q1), .q2(reg_file_1_q2));
  Comparator #(.width(32)) comparator_1 (.a(reg_file_1_q1), .b(reg_file_1_q2), .eq(branch_equal));  // open: gt, lt
  Multiplexer #(.width(32)) multiplexer_2 (
    .in0(reg_file_1_q1), .in1(pc_1_q), .out(multiplexer_2_out), .sel(set_pc_sel));
  Multiplexer #(.width(32)) multiplexer_3 (
    .in0(reg_file_1_q2), .in1(control_unit_1_imm), .out(multiplexer_3_out), .sel(imi_sel));
  Adder #(.width(32)) adder_1 (.a(multiplexer_2_out), .b(multiplexer_3_out), .out(adder_1_out));  // open: cin, cout
  RAM #(.addrWidth(24), .asyncread("true"), .dataWidth(32)) ram_1 (
    .addr(adder_1_out[25:2]), .we(store_sel), .oe(load_sel), .clk(clock_1_out), .din(reg_file_1_q2),
    .dout(ram_1_dout));

  // Notes on the sheet:
  //   contents of rom_1 (hex, n*v repeats v):
  //   11100293 22200313 628533 293 2a2a623 2c2a303 33300393 730663 128293 ffdff06f
endmodule

module pc (
  input  [31:0] d,
  input  clk,
  input  set_pc,
  output [31:0] q
);

  wire [31:0] adder_1_out, multiplexer_1_out;

  Register #(.width(32)) register_1 (.D(multiplexer_1_out), .en(1'b1), .clk(clk), .Q(q));  // open: clr
  Multiplexer #(.width(32)) multiplexer_1 (.in0(adder_1_out), .in1(d), .out(multiplexer_1_out), .sel(set_pc));
  Adder #(.width(32)) adder_1 (.a(q), .b(32'h4), .out(adder_1_out));  // open: cin, cout
endmodule

module reg_file (
  input  [31:0] d,
  input  [4:0] rd,
  input  [4:0] rs1,
  input  [4:0] rs2,
  input  clk,
  output [31:0] q1,
  output [31:0] q2
);

  wire decoder_1_out0, decoder_1_out1, decoder_1_out2, decoder_1_out3, decoder_1_out4, decoder_1_out5,
       decoder_1_out6, decoder_1_out7, decoder_1_out8, decoder_1_out9, decoder_1_out10, decoder_1_out11;
  wire [31:0] a0_q, a1_q, gp_q, ra_q, s0_q, s1_q, sp_q, t0_q, t1_q, t2_q, tp_q;

  Decoder #(.enable("false"), .select(5)) decoder_1 (
    .out0(decoder_1_out0), .out1(decoder_1_out1), .out2(decoder_1_out2), .out3(decoder_1_out3),
    .out4(decoder_1_out4), .out5(decoder_1_out5), .out6(decoder_1_out6), .out7(decoder_1_out7),
    .out8(decoder_1_out8), .out9(decoder_1_out9), .out10(decoder_1_out10), .out11(decoder_1_out11), .sel(rd));  // open: out12, out13, out14, out15, out16, out17, out18, out19, out20, out21, out22, out23, out24, out25, out26, out27, out28, out29, out30, out31
  // NoConnect on decoder_1_out0
  Register #(.width(32)) ra (.D(d), .en(decoder_1_out1), .clk(clk), .Q(ra_q));  // open: clr
  Register #(.width(32)) sp (.D(d), .en(decoder_1_out2), .clk(clk), .Q(sp_q));  // open: clr
  Register #(.width(32)) gp (.D(d), .en(decoder_1_out3), .clk(clk), .Q(gp_q));  // open: clr
  Register #(.width(32)) tp (.D(d), .en(decoder_1_out4), .clk(clk), .Q(tp_q));  // open: clr
  Register #(.width(32)) t0 (.D(d), .en(decoder_1_out5), .clk(clk), .Q(t0_q));  // open: clr
  Register #(.width(32)) t1 (.D(d), .en(decoder_1_out6), .clk(clk), .Q(t1_q));  // open: clr
  Register #(.width(32)) t2 (.D(d), .en(decoder_1_out7), .clk(clk), .Q(t2_q));  // open: clr
  Register #(.width(32)) s0 (.D(d), .en(decoder_1_out8), .clk(clk), .Q(s0_q));  // open: clr
  Register #(.width(32)) s1 (.D(d), .en(decoder_1_out9), .clk(clk), .Q(s1_q));  // open: clr
  Register #(.width(32)) a0 (.D(d), .en(decoder_1_out10), .clk(clk), .Q(a0_q));  // open: clr
  Register #(.width(32)) a1 (.D(d), .en(decoder_1_out11), .clk(clk), .Q(a1_q));  // open: clr
  Multiplexer #(.select(5), .width(32)) multiplexer_1 (
    .in0({32{1'b0}}), .in1(ra_q), .in2(sp_q), .in3(gp_q), .in4(tp_q), .in5(t0_q), .in6(t1_q), .in7(t2_q),
    .in8(s0_q), .in9(s1_q), .in10(a0_q), .in11(a1_q), .out(q1), .sel(rs1));  // open: in12, in13, in14, in15, in16, in17, in18, in19, in20, in21, in22, in23, in24, in25, in26, in27, in28, in29, in30, in31
  Multiplexer #(.select(5), .width(32)) multiplexer_2 (
    .in0({32{1'b0}}), .in1(ra_q), .in2(sp_q), .in3(gp_q), .in4(tp_q), .in5(t0_q), .in6(t1_q), .in7(t2_q),
    .in8(s0_q), .in9(s1_q), .in10(a0_q), .in11(a1_q), .out(q2), .sel(rs2));  // open: in12, in13, in14, in15, in16, in17, in18, in19, in20, in21, in22, in23, in24, in25, in26, in27, in28, in29, in30, in31
endmodule

module control_unit (
  input  branch_equal,
  input  [31:0] inst,
  output [4:0] rd,
  output [4:0] rs1,
  output [4:0] rs2,
  output imi_sel,
  output load_sel,
  output store_sel,
  output set_pc_sel,
  output [31:0] imm
);

  wire and_1_out, and_4_out, and_5_out, and_6_out, not_1_out, not_3_out, not_4_out, not_5_out, not_6_out,
       not_7_out, not_8_out, not_9_out, not_10_out;
  wire [2:0] multiplexer_1_out;

  Multiplexer #(.width(3)) multiplexer_1 (.in0(inst[6:4]), .in1(inst[5:3]), .out(multiplexer_1_out), .sel(inst[6]));
  not not_1 (not_1_out, multiplexer_1_out[2]);
  and and_1 (and_1_out, not_1_out, multiplexer_1_out[1], multiplexer_1_out[0]);
  not not_2 (imi_sel, and_1_out);
  Multiplexer #(.select(3), .width(32)) multiplexer_2 (
    .in0({{20{1'b0}}, inst[31:20]}), .in1({{20{1'b0}}, inst[31:20]}),
    .in2({{20{1'b0}}, inst[31:25], inst[11:7]}), .in3({32{1'b0}}),
    .in4({{20{inst[31]}}, inst[7], inst[30:25], inst[11:8], 1'b0}),
    .in5({{12{inst[31]}}, inst[19:12], inst[20], inst[30:21], 1'b0}), .out(imm), .sel(multiplexer_1_out));  // open: in6, in7
  not not_3 (not_3_out, multiplexer_1_out[2]);
  not not_4 (not_4_out, multiplexer_1_out[1]);
  not not_5 (not_5_out, multiplexer_1_out[0]);
  and and_2 (load_sel, not_3_out, not_4_out, not_5_out);
  not not_6 (not_6_out, multiplexer_1_out[2]);
  not not_7 (not_7_out, multiplexer_1_out[0]);
  and and_3 (store_sel, not_6_out, multiplexer_1_out[1], not_7_out);
  not not_8 (not_8_out, multiplexer_1_out[1]);
  and and_4 (and_4_out, multiplexer_1_out[2], not_8_out, not_9_out);
  not not_9 (not_9_out, multiplexer_1_out[0]);
  not not_10 (not_10_out, multiplexer_1_out[1]);
  and and_5 (and_5_out, multiplexer_1_out[2], not_10_out, multiplexer_1_out[0]);
  and and_6 (and_6_out, and_4_out, branch_equal);
  or or_1 (set_pc_sel, and_6_out, and_5_out);

  assign rd = inst[11:7];
  assign rs1 = inst[19:15];
  assign rs2 = inst[24:20];
endmodule
